// Logisim project 3.2_BancRegsBiport+PC.circ as structural Verilog: 4 circuits, main circuit main
module main (
  input  Load,
  input  Increment,
  input  Write
);

  wire Reset_2_out, Reset_out, Sincro_2_out, Sincro_out;
  wire [1:0] IN_out, out1_out, out2_out;
  wire [7:0] bancregistres4x8b_1_regout1, bancregistres4x8b_1_regout2, Data_IN_out, New_PC_value_out,
       pc8bits_1_pcout;

  Button Sincro (.out(Sincro_out));
  Button Reset (.out(Reset_out));
  Slider #(.value('hc4)) Data_IN (.out(Data_IN_out));
  Slider #(.width(2), .value('h3)) IN (.out(IN_out));
  Slider #(.width(2), .value('h2)) out1 (.out(out1_out));
  Slider #(.width(2), .value('h3)) out2 (.out(out2_out));
  BancRegistres4x8b bancregistres4x8b_1 (
    .RegIn(Data_IN_out), .\NúmRegIn (IN_out), .Wr(Write), .Sinc(Sincro_out), .Reset(Reset_out),
    .RegOut1(bancregistres4x8b_1_regout1), .RegOut2(bancregistres4x8b_1_regout2), .\NúmRegOut2 (out2_out),
    .\NúmRegOut1 (out1_out));
  // Probe on bancregistres4x8b_1_regout2
  // Probe on bancregistres4x8b_1_regout1
  Button Sincro_2 (.out(Sincro_2_out));
  Slider #(.value('hf0)) New_PC_value (.out(New_PC_value_out));
  PC8bits pc8bits_1 (
    .NewPC(New_PC_value_out), .Sinc(Sincro_2_out), .Reset(Reset_2_out), .PCout(pc8bits_1_pcout),
    .Inc(Increment), .Load(Load));
  // Probe on pc8bits_1_pcout
  Button Reset_2 (.out(Reset_2_out));

  // Notes on the sheet:
  //   PractFC3.2 Equip XI13$Eric García Castro$Iván Molinero Moreno
endmodule

module BancRegistres4x8b (
  input  [7:0] RegIn,
  input  Wr,
  input  Sinc,
  input  Reset,
  input  [1:0] \NúmRegIn ,
  input  [1:0] \NúmRegOut1 ,
  input  [1:0] \NúmRegOut2 ,
  output [7:0] RegOut1,
  output [7:0] RegOut2
);

  wire demultiplexer_1_out0, demultiplexer_1_out1, demultiplexer_1_out2, demultiplexer_1_out3;
  wire [7:0] R0_dout, R1_dout, R2_dout, R3_dout;

  Demultiplexer #(.select(2), .enable("false")) demultiplexer_1 (
    .out0(demultiplexer_1_out0), .out1(demultiplexer_1_out1), .out2(demultiplexer_1_out2),
    .out3(demultiplexer_1_out3), .in(Sinc), .sel(\NúmRegIn ));
  Registre8bits R0 (.Wr(Wr), .Sinc(demultiplexer_1_out0), .Reset(Reset), .Din(RegIn), .Dout(R0_dout));
  Registre8bits R1 (.Wr(Wr), .Sinc(demultiplexer_1_out1), .Reset(Reset), .Din(RegIn), .Dout(R1_dout));
  Registre8bits R2 (.Wr(Wr), .Sinc(demultiplexer_1_out2), .Reset(Reset), .Din(RegIn), .Dout(R2_dout));
  Registre8bits R3 (.Wr(Wr), .Sinc(demultiplexer_1_out3), .Reset(Reset), .Din(RegIn), .Dout(R3_dout));
  Multiplexer #(.select(2), .width(8), .enable("false")) multiplexer_1 (
    .in0(R0_dout), .in1(R1_dout), .in2(R2_dout), .in3(R3_dout), .out(RegOut1), .sel(\NúmRegOut1 ));
  Multiplexer #(.select(2), .width(8), .enable("false")) multiplexer_2 (
    .in0(R0_dout), .in1(R1_dout), .in2(R2_dout), .in3(R3_dout), .out(RegOut2), .sel(\NúmRegOut2 ));
endmodule

module PC8bits (
  input  [7:0] NewPC,
  input  Inc,
  input  Reset,
  input  Load,
  input  Sinc,
  output [7:0] PCout
);

  wire xor_1_out;
  wire [7:0] adder_1_out, multiplexer_1_out;

  Adder adder_1 (.a(8'h1), .b(PCout), .out(adder_1_out));  // open: cin, cout
  xor xor_1 (xor_1_out, Inc, Load);
  Multiplexer #(.width(8), .enable("false")) multiplexer_1 (
    .in0(adder_1_out), .in1(NewPC), .out(multiplexer_1_out), .sel(Load));
  Registre8bits PC___R15 (.Wr(xor_1_out), .Sinc(Sinc), .Reset(Reset), .Din(multiplexer_1_out), .Dout(PCout));
endmodule

module Registre8bits (
  input  [7:0] Din,
  input  Wr,
  input  Sinc,
  input  Reset,
  output [7:0] Dout
);

  Register #(.Select("low")) Reg8b (.D(Din), .en(Wr), .Q(Dout), .clk(Sinc), .clr(Reset));
endmodule
